// Logisim project contador_decre.circ as structural Verilog: 1 circuit, main circuit main
module main (
  input  in_1,
  output [2:0] out_2
);

  wire clock_1_out;

  Clock clock_1 (.out(clock_1_out));
  T_Flip_Flop t_ff_1 (.T(in_1), .clk(clock_1_out), .Q(out_2[0]));  // open: Qn, reset, preset
  T_Flip_Flop t_ff_2 (.T(in_1), .clk(out_2[0]), .Q(out_2[1]));  // open: Qn, reset, preset
  T_Flip_Flop t_ff_3 (.T(in_1), .clk(out_2[1]), .Q(out_2[2]));  // open: Qn, reset, preset
endmodule
